# Fritzing sketch WiggleBinLight (saved by Fritzing 0.9.10b)
breadboards: 1

parts:
  Power_RGB1 = Prolight RGB 3 Watt Star
  R1 = Resistor [tolerance=±5% power=0.25 resistance=1k package=THT]
  R2 = Resistor [tolerance=±5% power=0.25 resistance=10k package=THT]
  Q1S8050 = NPN-Transistor [package="TO92 [THT]"]
  U1 = ATTINY45 [package=dip]

nets:
  N1: Power_RGB1.R+, U1.PB5(NRES), U1.VCC
  N2: R1.Pin_0, R2.Pin_1, Q1S8050.C
  N3: R1.Pin_1, U1.PB4(ADC2), U1.PB1(MISO)
  N4: R2.Pin_0, Q1S8050.E, U1.GND, U1.PB0(MOSI)
  N5: U1.PB3(ADC3), U1.PB2(SCK_ADC1)
